# Fritzing sketch Payload ServoMotor Circuit Sketch3 (saved by Fritzing 0.9.3b)
breadboards: 1

parts:
  Part1 = Arduino Uno (Rev3)
  R1 = Resistor [tolerance=±5% resistance=220 package=THT]
  R2 = Resistor [tolerance=±5% resistance=220 package=THT]  # not connected
  LED1 = RGB LED (com. cathode, rgb) [package="5 mm [THT]"]
  SPKR1 = Loudspeaker
  C1 = Electrolytic Capacitor [capacitance=1000μF package="1010 [SMD, electrolytic]"]
  J1 = Basic Servo
  S2 = Round Pushbutton
  BAT1 = BC9VPC [package=bc9vpc]  # not connected

nets:
  GND: Part1.GND, LED1.blue_anode, SPKR1.pin1, C1.+, J1.gnd
  N1: Part1.D2, S2.leg0
  N2: Part1.D3_PWM, J1.pulse
  N3: Part1.D4, R1.Pin_0
  N4: Part1.D5_PWM, SPKR1.pin2
  5V: Part1.5V, J1.vcc
  N5: R1.Pin_1, LED1.red_anode
